# Fritzing sketch schema (saved by Fritzing 1.0.2b)
breadboards: 1

parts:
  Composant1 = Arduino Uno (Rev3) - ICSP
  U1 = POT [knob_status=50% power=0.5W package=pot_alpha_rv16af-20]
  J1 = Basic Servo

nets:
  GND: Composant1.A0, Composant1.GND, U1.S, U1.E, J1.gnd
  N1: Composant1.D9_PWM, J1.pulse
  5V: Composant1.5V, U1.A, J1.vcc
